# Fritzing sketch Alarm (saved by Fritzing 1.0.0rc)
breadboards: 1

parts:
  Part1 = Arduino Mega 2560 (Rev3)
  ZS-042_RTC1 = ZS-042 RTC Module  # not connected
  LCD1 = LCD screen
  R1 = Rotary Potentiometer (Large) [maximum_resistance=10kΩ knob_status=50% power=0.5W package=THT]
  R2 = Resistor [tolerance=±5% resistance=220 package="1206 [SMD]"]

nets:
  N1: Part1.D12_PWM, LCD1.RS
  N2: Part1.D11_PWM, LCD1.E
  5V: Part1.5V, LCD1.VDD, R1.leg2, R2.Pin_0
  GND: Part1.GND, LCD1.VSS, LCD1.R/W, LCD1.LED-, R1.leg1
  N3: Part1.D2_PWM, LCD1.DB4
  N4: Part1.D3_PWM, LCD1.DB5
  N5: Part1.D4_PWM, LCD1.DB6
  N6: Part1.D5_PWM, LCD1.DB7
  N7: LCD1.V0, R1.wiper
  N8: LCD1.LED+, R2.Pin_1
